# Fritzing sketch Untitled Sketch (saved by Fritzing 0.9.3b)

parts:
  Raspberry_Pi_1 = Raspberry Pi 3 [part_number=RPI-3-V1.2]
  J1 = Basic Servo  # not connected
  J6 = Basic Servo  # not connected
  J8 = Basic Servo  # not connected
  J9 = Basic Servo  # not connected
  J10 = Basic Servo  # not connected
  J11 = Basic Servo  # not connected
  J12 = Basic Servo  # not connected
  J13 = Basic Servo  # not connected
  J14 = Basic Servo  # not connected
  J15 = Basic Servo  # not connected
  J16 = Basic Servo  # not connected
  J17 = Basic Servo  # not connected
  J18 = Basic Servo  # not connected
  J19 = Basic Servo  # not connected
  hc-sr1 = hc-sr04
  DHT1 = DHT22 Humidity and Temperature Sensor
  R1 = Resistor [tolerance=±5% resistance=220 package=THT]
  CAMERA1 = TTL Serial JPEG Camera  # not connected
  Composant1 = MQ-9 breakout  # not connected

nets:
  3V3: Raspberry_Pi_1.3v3, hc-sr1.VCC, DHT1.VDD, R1.Pin_0
  N1: Raspberry_Pi_1.GPIO4, DHT1.DATA, R1.Pin_1
  GND: Raspberry_Pi_1.GND, hc-sr1.GND, DHT1.NULL, DHT1.GND
  N2: Raspberry_Pi_1.GPIO23, hc-sr1.Echo
  N3: Raspberry_Pi_1.GPIO18, hc-sr1.Trig

notes:
  Pan/Tilt Assembly
  Spider legs
  MototPi3
  Raspberry Pi 3+
  Capteur Ultrason
  Module PiCamera
  Capteur CO
  Capteur CO2 / COCP
  Capteur Temp/Humi

custom parts:
  TTL Serial JPEG Camera: TTL Serial JPEG Camera with NTSC Out
  MQ-9 breakout: SKU: 101284
